# Fritzing sketch DCS Instrument WiFi Controller (saved by Fritzing 0.9.3b)
breadboards: 1

parts:
  U1 = NodeMCU V3.0
  OLED1 = 128x64 Monochrom OLED Display with SPI Control
  BB1 = 4-Line Bi-Directional Level Shifter

nets:
  N1: U1.D1, BB1.A1
  N2: U1.D2, BB1.A2
  N3: U1.D3, OLED1.Reset
  N4: U1.D4, OLED1.SA0/DC
  3V3: U1.3V3, OLED1.3v3, BB1.LV
  GND: U1.GND, OLED1.GND, BB1.GND
  N5: U1.D5, OLED1.Clock
  N6: U1.D7, OLED1.Data
  N7: U1.D8, OLED1.CS
  N8: U1.Vin, BB1.HV

notes:
  Data = MOSI
  Lower power rails are +5v and upper rails are +3.3v. The actual board (and the i2c bus) is powered by a DC-DC buck converter.

custom parts:
  NodeMCU V3.0: ESP8266 based NodeMCU
  4-Line Bi-Directional Level Shifter: 4-Channel Bi-Directional Level Shifter
